# Fritzing sketch SenseoWifi-PCB (saved by Fritzing 0.9.4)
circuit board: 3.42054cm x 7.50272cm

parts:
  R3 = Resistor [tolerance=±5% resistance=150 package=THT]
  R2 = Resistor [tolerance=±5% resistance=1.5k package=THT]
  R1 = Resistor [tolerance=±5% resistance=470 package=THT]
  R1_2 = Resistor [tolerance=±5% resistance=470 package=THT]
  T1_____T2_____TP = male pin header, 3 pins [form="♂ (male)"]
  GND = male pin header, 1 pin [form="♂ (male)"]
  LED = male pin header, 1 pin [form="♂ (male)"]
  R1_3 = Resistor [tolerance=±5% resistance=470 package=THT]
  Buzzer = Buzzer 12mm [package=buzzer-12mm-ns-kit]
  J1 = male pin header, 8 pins [form="♂ (male)"]
  J2 = male pin header, 7 pins [form="♂ (male)"]
  WeMos_D1_Mini = WeMos D1 Mini
  TCRT = male pin header, 4 pins [form="♂ (male)"]
  U1 = Sharp PC817 [package=THT]
  U2 = Sharp PC817 [package=THT]
  U3 = Sharp PC817 [package=THT]
  U4 = Sharp PC817 [package=THT]
  J3_ConfigReset = male pin header, 2 pins [form="♂ (male)"]
  J4_Power = male pin header, 2 pins [form="♂ (male)"]

nets:
  N1: R3.Pin_0, J1.pin2, WeMos_D1_Mini.D8
  N2: R3.Pin_1, Buzzer.1
  N3: R2.Pin_0, LED.pin1
  N4: R2.Pin_1, U1.Pin_1
  T1_OC-in: R1.Pin_0, J1.pin5, WeMos_D1_Mini.D5
  N5: R1.Pin_1, U4.Pin_1
  TP_OC-in: R1_2.Pin_0, J2.pin5, WeMos_D1_Mini.D1
  N6: R1_2.Pin_1, U2.Pin_1
  N7: T1_____T2_____TP.pin1, U4.Pin_4
  N8: T1_____T2_____TP.pin2, U3.Pin_4
  N9: T1_____T2_____TP.pin3, U2.Pin_4
  N10: GND.pin1, U1.Pin_2, U2.Pin_3, U3.Pin_3, U4.Pin_3
  T2_OC-in: R1_3.Pin_0, J2.pin4, WeMos_D1_Mini.D2
  N11: R1_3.Pin_1, U3.Pin_1
  GND: Buzzer.2, J2.pin1, WeMos_D1_Mini.G, TCRT.pin2, U1.Pin_3, U2.Pin_2, U3.Pin_2, U4.Pin_2, J3_ConfigReset.pin1, J4_Power.pin2
  N12: J1.pin1, WeMos_D1_Mini.3V3
  LED_OC-out: J1.pin3, WeMos_D1_Mini.D7, U1.Pin_4
  N13: J1.pin4, WeMos_D1_Mini.D6, TCRT.pin3
  N14: J1.pin6, WeMos_D1_Mini.D0
  N15: J1.pin7, WeMos_D1_Mini.A0, TCRT.pin4
  N16: J1.pin8, WeMos_D1_Mini.RST
  N17: J2.pin2, WeMos_D1_Mini.D4, J3_ConfigReset.pin2
  N18: J2.pin3, WeMos_D1_Mini.D3
  N19: J2.pin6, WeMos_D1_Mini.RX
  N20: J2.pin7, WeMos_D1_Mini.TX
  N21: WeMos_D1_Mini.5V, TCRT.pin1, J4_Power.pin1

notes:
  Senseo Connections
  SenseoWifi - PCB v1.8
  http://github.com/ThomDietrich/SenseoWifi
  G  D4  D3  D2  D1  RX  TX
  A   D   G   V
  3V3 D8  D7  D6  D5  D0  A0 RST
  Breadboard view not used
  Check out circuit and pcb layout view
  ----------------
  4x PC817
  3V3  D8  D7  D6  D5  D0  A0  RST
  G  CR
  G  D3
  5V  G
  J4  J3
